# Fritzing sketch PixelBrite PCB v1 (saved by Fritzing 0.7.12b)
breadboards: 1

parts:
  part = female pin header, 5 pins [form="♀ (female)"]
  part_2 = female pin header, 4 pins [form="♀ (female)"]
  part_3 = female pin header, 2 pins [form="♀ (female)"]
  part_4 = female pin header, 4 pins [form="♀ (female)"]
  part_5 = female pin header, 6 pins [form="♀ (female)"]
  J93 = female pin header, 3 pins [form="♀ (female)"]
  part_6 = female pin header, 5 pins [form="♀ (female)"]
  part_7 = female pin header, 5 pins [form="♀ (female)"]
  part_8 = female pin header, 3 pins [form="♀ (female)"]
  Teensy2 = Teensy 2.0
  microSD3 = MicroSD Breakout
  Power_Switch = Toggle Switch [package=THT]
  PushButton = Pushbutton [package=THT]
  5V_DC_Input = 2.1mm Barrel Jack with Terminal Block
  Screw_Terminal = screw terminal, 4 pins
  Molex_Connector = Generic female header - metal rounded - 6 pins [package=THT]
  Pull_Up_Resistor = 10k Ω Resistor [package=THT]

nets:
  N1: part.pin1, part_7.pin5
  N2: part.pin2, part_7.pin4
  N3: part.pin3, part_7.pin3
  N4: part.pin4, part_7.pin2
  N5: part.pin5, part_3.pin2, part_5.pin1
  N6: part_2.pin1, part_4.pin3
  N7: part_2.pin2, part_4.pin4
  N8: part_2.pin4, part_3.pin1
  N9: part_4.pin1, part_5.pin2, part_5.pin6, part_8.pin3
  N10: part_5.pin3, part_5.pin4
  N11: part_5.pin5, J93.pin1, part_7.pin1
  N12: J93.pin2, part_6.pin1
  GND: Teensy2.GND, microSD3.GND, 5V_DC_Input.NEG, Screw_Terminal.pin2, Molex_Connector.pin2, Pull_Up_Resistor.Pin_1
  N13: Teensy2.B1, Screw_Terminal.pin4
  N14: Teensy2.B2, Screw_Terminal.pin3
  N15: Teensy2.D1, microSD3.CS
  N16: Teensy2.D2, microSD3.CLK
  N17: Teensy2.D3, microSD3.MOSI
  N18: Teensy2.C6, microSD3.MISO
  N19: Teensy2.VCC, PushButton.leg1, Molex_Connector.pin1, Molex_Connector.pin5
  N20: microSD3.5V, PushButton.leg0, Screw_Terminal.pin1, Molex_Connector.pin6, Pull_Up_Resistor.Pin_0
  VCC: Power_Switch.COM, 5V_DC_Input.POS, Molex_Connector.pin3, Molex_Connector.pin4

notes:
  LeoneLabs
  PixelBrite
  V2
  CLK
  DATA
  GND
  VCC
  BUT-
  BUT+
  SW-
  SW+
  7 (INT2)
  5 (INT0)
  5V
  6 (INT1)
  2 (B2)
  1 (B1)
  SS
  MISO
  MOSI
  SW
  NC
  8 (INT3)
  9

custom parts:
  MicroSD Breakout: 5V-ready microSD Breakout with Level Shifter
